// Logisim project 2B-counter.circ as structural Verilog: 1 circuit, main circuit main
module main (
  input  Q0,
  input  Q1,
  input  INC,
  input  CLR,
  output N1,
  output N0
);

  wire and_1_out, and_2_out, and_3_out, and_4_out;

  and and_1 (and_1_out, INC, Q0);
  and and_2 (and_2_out, ~CLR, ~INC, Q1);  // AND_Gate
  and and_3 (and_3_out, INC, ~Q1);  // AND_Gate
  and and_4 (and_4_out, ~CLR, ~INC, Q0);  // AND_Gate
  or or_1 (N1, and_1_out, and_2_out);
  or or_2 (N0, and_3_out, and_4_out);
endmodule
