// Logisim project 3bitCounter.circ as structural Verilog: 1 circuit, main circuit main
module main (
  input  CLK
);

  wire d_ff_1_q, d_ff_2_q, d_ff_3_q, not_1_out, not_2_out;

  not not_1 (not_1_out, d_ff_1_q);
  D_Flip_Flop d_ff_1 (.clk(CLK), .D(d_ff_3_q), .Q(d_ff_1_q));  // open: Qn, preset, en, reset
  D_Flip_Flop d_ff_2 (.clk(CLK), .D(not_1_out), .Q(d_ff_2_q));  // open: Qn, preset, en, reset
  not not_2 (not_2_out, d_ff_2_q);
  D_Flip_Flop d_ff_3 (.clk(CLK), .D(not_2_out), .Q(d_ff_3_q));  // open: Qn, preset, en, reset
endmodule
