// Logisim project 4bit_8word_Reg-replace.circ as structural Verilog: 4 circuits, main circuit main
module main (
  input  In_0,
  input  In_1,
  input  In_2,
  input  In_3,
  input  Clock_input,
  input  A0,
  input  A1,
  input  A2,
  input  WE,
  output OUT_0,
  output OUT_1,
  output OUT_2,
  output OUT_3
);

  wire decoder_1_out_0, decoder_1_out_1, decoder_1_out_2, decoder_1_out_3, decoder_1_out_4, decoder_1_out_5,
       decoder_1_out_6, decoder_1_out_7;
  wire [3:0] Output_0, Output_1, Output_2, Output_3, Output_4, Output_5, Output_6, Output_7;

  Decoder decoder_1 (
    .A0(A0), .A1(A1), .A2(A2), .WE(WE), .Out_0(decoder_1_out_0), .Out_1(decoder_1_out_1),
    .Out_2(decoder_1_out_2), .Out_3(decoder_1_out_3), .Out_4(decoder_1_out_4), .Out_5(decoder_1_out_5),
    .Out_6(decoder_1_out_6), .Out_7(decoder_1_out_7));
  _4Bit_Register u_4bit_register_1 (
    .ln_0(In_0), .ln_1(In_1), .ln_2(In_2), .ln_3(In_3), .CLK(Clock_input), .WE(decoder_1_out_0),
    .Out_0(Output_0[0]), .Out_1(Output_0[1]), .Out_2(Output_0[2]), .Out_3(Output_0[3]));
  _4Bit_Register u_4bit_register_2 (
    .ln_0(In_0), .ln_1(In_1), .ln_2(In_2), .ln_3(In_3), .CLK(Clock_input), .WE(decoder_1_out_2),
    .Out_0(Output_2[0]), .Out_1(Output_2[1]), .Out_2(Output_2[2]), .Out_3(Output_2[3]));
  _4Bit_Register u_4bit_register_3 (
    .ln_0(In_0), .ln_1(In_1), .ln_2(In_2), .ln_3(In_3), .CLK(Clock_input), .WE(decoder_1_out_4),
    .Out_0(Output_4[0]), .Out_1(Output_4[1]), .Out_2(Output_4[2]), .Out_3(Output_4[3]));
  _4Bit_Register u_4bit_register_4 (
    .ln_0(In_0), .ln_1(In_1), .ln_2(In_2), .ln_3(In_3), .CLK(Clock_input), .WE(decoder_1_out_6),
    .Out_0(Output_6[0]), .Out_1(Output_6[1]), .Out_2(Output_6[2]), .Out_3(Output_6[3]));
  _4Bit_Register u_4bit_register_5 (
    .ln_0(In_0), .ln_1(In_1), .ln_2(In_2), .ln_3(In_3), .CLK(Clock_input), .WE(decoder_1_out_1),
    .Out_0(Output_1[0]), .Out_1(Output_1[1]), .Out_2(Output_1[2]), .Out_3(Output_1[3]));
  _4Bit_Register u_4bit_register_6 (
    .ln_0(In_0), .ln_1(In_1), .ln_2(In_2), .ln_3(In_3), .CLK(Clock_input), .WE(decoder_1_out_3),
    .Out_0(Output_3[0]), .Out_1(Output_3[1]), .Out_2(Output_3[2]), .Out_3(Output_3[3]));
  _4Bit_Register u_4bit_register_7 (
    .ln_0(In_0), .ln_1(In_1), .ln_2(In_2), .ln_3(In_3), .CLK(Clock_input), .WE(decoder_1_out_5),
    .Out_0(Output_5[0]), .Out_1(Output_5[1]), .Out_2(Output_5[2]), .Out_3(Output_5[3]));
  _4Bit_Register u_4bit_register_8 (
    .ln_0(In_0), .ln_1(In_1), .ln_2(In_2), .ln_3(In_3), .CLK(Clock_input), .WE(decoder_1_out_7),
    .Out_0(Output_7[0]), .Out_1(Output_7[1]), .Out_2(Output_7[2]), .Out_3(Output_7[3]));
  Multiplexer #(.select(3), .width(4), .enable("false")) multiplexer_1 (
    .in0(Output_0), .in1(Output_1), .in2(Output_2), .in3(Output_3), .in4(Output_4), .in5(Output_5),
    .in6(Output_6), .in7(Output_7), .out({OUT_3, OUT_2, OUT_1, OUT_0}), .sel({A2, A1, A0}));

  // Other names for the same wires on the sheet: Input[4:0] = {Clock_input, In_3, In_2, In_1, In_0}
endmodule

module _1_Bit_register (
  input  CLK,
  input  Data_In,
  input  WE,
  output Data_Out
);

  wire multiplexer_1_out;

  Multiplexer #(.enable("false")) multiplexer_1 (.in0(Data_Out), .in1(Data_In), .out(multiplexer_1_out), .sel(WE));
  D_Flip_Flop d_ff_1 (.clk(CLK), .D(multiplexer_1_out), .Q(Data_Out));  // open: Qn, preset, en, reset
endmodule

module _4Bit_Register (
  input  ln_0,
  input  ln_1,
  input  ln_2,
  input  ln_3,
  input  CLK,
  input  WE,
  output Out_0,
  output Out_1,
  output Out_2,
  output Out_3
);

  _1_Bit_register u_1_bit_register_1 (.CLK(CLK), .Data_In(ln_0), .Data_Out(Out_0), .WE(WE));
  _1_Bit_register u_1_bit_register_2 (.CLK(CLK), .Data_In(ln_1), .Data_Out(Out_1), .WE(WE));
  _1_Bit_register u_1_bit_register_3 (.CLK(CLK), .Data_In(ln_2), .Data_Out(Out_2), .WE(WE));
  _1_Bit_register u_1_bit_register_4 (.CLK(CLK), .Data_In(ln_3), .Data_Out(Out_3), .WE(WE));
endmodule

module Decoder (
  input  A0,
  input  A1,
  input  A2,
  input  WE,
  output Out_0,
  output Out_1,
  output Out_2,
  output Out_3,
  output Out_4,
  output Out_5,
  output Out_6,
  output Out_7
);

  wire not_1_out, not_2_out, not_3_out;

  not not_1 (not_1_out, A0);
  not not_2 (not_2_out, A1);
  not not_3 (not_3_out, A2);
  and _0 (Out_0, not_1_out, not_2_out, not_3_out, WE);
  and _1 (Out_1, A0, not_2_out, not_3_out, WE);
  and _2 (Out_2, not_1_out, A1, not_3_out, WE);
  and _3 (Out_3, A0, A1, not_3_out, WE);
  and _4 (Out_4, not_1_out, not_2_out, A2, WE);
  and _5 (Out_5, A0, not_2_out, A2, WE);
  and _6 (Out_6, not_1_out, A1, A2, WE);
  and _7 (Out_7, A0, A1, A2, WE);
endmodule
