// Logisim project 4bit_ALU-replace.circ as structural Verilog: 6 circuits, main circuit main
module main (
  input  A0,
  input  A1,
  input  A2,
  input  A3,
  input  B0,
  input  B1,
  input  B2,
  input  B3,
  input  S0,
  input  S1,
  output OUT_0,
  output OUT_1,
  output OUT_2,
  output OUT_3
);

  wire ADD_0, ADD_1, ADD_2, ADD_3, AND_0, AND_1, AND_2, AND_3, OR_0, OR_1, OR_2, OR_3, XOR_0, XOR_1, XOR_2,
       XOR_3;

  XOR u_xor_1 (.in_1({A0, A1, A2, A3}), .in_2({B0, B1, B2, B3}), .out_3({XOR_0, XOR_1, XOR_2, XOR_3}));
  AND u_and_1 (.in_1({A0, A1, A2, A3}), .in_2({B0, B1, B2, B3}), .out_3({AND_3, AND_2, AND_1, AND_0}));
  OR u_or_1 (.in_1({A0, A1, A2, A3}), .in_2({B0, B1, B2, B3}), .out_3({OR_3, OR_2, OR_1, OR_0}));
  _4bit_Adder u_4bit_adder_1 (
    .A0(A0), .A1(A1), .A2(A2), .A3(A3), .B0(B0), .B1(B1), .B2(B2), .B3(B3), .Out_0(ADD_0), .Out_1(ADD_1),
    .Out_2(ADD_2), .Out_3(ADD_3));
  Multiplexer #(.select(2), .enable("false")) multiplexer_1 (
    .in0(XOR_0), .in1(AND_0), .in2(OR_0), .in3(ADD_0), .out(OUT_0), .sel({S1, S0}));
  Multiplexer #(.select(2), .enable("false")) multiplexer_2 (
    .in0(XOR_1), .in1(AND_1), .in2(OR_1), .in3(ADD_1), .out(OUT_1), .sel({S1, S0}));
  Multiplexer #(.select(2), .enable("false")) multiplexer_3 (
    .in0(XOR_2), .in1(AND_2), .in2(OR_2), .in3(ADD_2), .out(OUT_2), .sel({S1, S0}));
  Multiplexer #(.select(2), .enable("false")) multiplexer_4 (
    .in0(XOR_3), .in1(AND_3), .in2(OR_3), .in3(ADD_3), .out(OUT_3), .sel({S1, S0}));

  // Other names for the same wires on the sheet: A[3:0] = {A0, A1, A2, A3}; B[3:0] = {B0, B1, B2, B3}
endmodule

module OR (
  input  [3:0] in_1,
  input  [3:0] in_2,
  output [3:0] out_3
);

  or or_1 (out_3[0], in_1[3], in_2[3]);
  or or_2 (out_3[1], in_1[2], in_2[2]);
  or or_3 (out_3[2], in_1[1], in_2[1]);
  or or_4 (out_3[3], in_1[0], in_2[0]);

  // Other names for the same wires on the sheet: A3 = in_1[0]; A2 = in_1[1]; A1 = in_1[2]; A0 = in_1[3]; B3 = in_2[0];
  //   B2 = in_2[1]; B1 = in_2[2]; B0 = in_2[3]
endmodule

module AND (
  input  [3:0] in_1,
  input  [3:0] in_2,
  output [3:0] out_3
);

  and and_1 (out_3[0], in_1[3], in_2[3]);
  and and_2 (out_3[1], in_1[2], in_2[2]);
  and and_3 (out_3[2], in_1[1], in_2[1]);
  and and_4 (out_3[3], in_1[0], in_2[0]);

  // Other names for the same wires on the sheet: A3 = in_1[0]; A2 = in_1[1]; A1 = in_1[2]; A0 = in_1[3]; B3 = in_2[0];
  //   B2 = in_2[1]; B1 = in_2[2]; B0 = in_2[3]
endmodule

module XOR (
  input  [3:0] in_1,
  input  [3:0] in_2,
  output [3:0] out_3
);

  xor xor_1 (out_3[3], in_1[3], in_2[3]);
  xor xor_2 (out_3[2], in_1[2], in_2[2]);
  xor xor_3 (out_3[1], in_1[1], in_2[1]);
  xor xor_4 (out_3[0], in_1[0], in_2[0]);

  // Other names for the same wires on the sheet: A3 = in_1[0]; A2 = in_1[1]; A1 = in_1[2]; A0 = in_1[3]; B3 = in_2[0];
  //   B2 = in_2[1]; B1 = in_2[2]; B0 = in_2[3]
endmodule

module _1Bit_Adder (
  input  A,
  input  B,
  input  Cin,
  output S,
  output Cout
);

  wire and_1_out, and_2_out, and_3_out;

  xor xor_1 (S, A, B, Cin);
  and and_1 (and_1_out, A, B);
  and and_2 (and_2_out, B, Cin);
  and and_3 (and_3_out, Cin, A);
  or or_1 (Cout, and_1_out, and_2_out, and_3_out);
endmodule

// 4Bit-Adder
module _4bit_Adder (
  input  A0,
  input  A1,
  input  A2,
  input  A3,
  input  B0,
  input  B1,
  input  B2,
  input  B3,
  output Out_0,
  output Out_1,
  output Out_2,
  output Out_3
);

  wire C0, C1, C2;

  _1Bit_Adder u_1bit_adder_1 (.A(A0), .B(B0), .Cin(1'b0), .S(Out_0), .Cout(C0));
  _1Bit_Adder u_1bit_adder_2 (.A(A1), .B(B1), .Cin(C0), .S(Out_1), .Cout(C1));
  _1Bit_Adder u_1bit_adder_3 (.A(A2), .B(B2), .Cin(C1), .S(Out_2), .Cout(C2));
  _1Bit_Adder u_1bit_adder_4 (.A(A3), .B(B3), .Cin(C2), .S(Out_3));  // open: Cout
endmodule
