// Logisim project 8to1MUX-replace (2).circ as structural Verilog: 1 circuit, main circuit main
module main (
  input  In0,
  input  In1,
  input  In2,
  input  In3,
  input  In4,
  input  In5,
  input  In6,
  input  In7,
  input  S2,
  input  S1,
  input  S0,
  output Out
);

  wire multiplexer_1_out, multiplexer_2_out;

  Multiplexer #(.select(2), .enable("false")) multiplexer_1 (
    .in0(In0), .in1(In1), .in2(In2), .in3(In3), .out(multiplexer_1_out), .sel({S1, S0}));
  Multiplexer #(.select(2), .enable("false")) multiplexer_2 (
    .in0(In4), .in1(In5), .in2(In6), .in3(In7), .out(multiplexer_2_out), .sel({S1, S0}));
  Multiplexer #(.select(2), .enable("false")) multiplexer_3 (
    .in0(multiplexer_1_out), .in1(multiplexer_1_out), .in2(multiplexer_2_out), .in3(multiplexer_2_out),
    .out(Out), .sel({2{S2}}));
endmodule
