// Logisim project Final (2).circ as structural Verilog: 11 circuits, main circuit main
module main (
  input  CLR
);

  wire CLK, DWE, SUB, WE;
  wire [1:0] AFS, RSS;
  wire [2:0] Addr_A, Addr_B, Addr_D;
  wire [3:0] ALU, multiplexer_1_out, Opcode, Port_A, Port_B;
  wire [3:3] Data;
  wire [7:0] counter_1_q;
  wire [7:7] rom_2_data;
  wire [11:7] rom_1_data;

  Clock clock_1 (.out(CLK));
  Counter counter_1 (.Q(counter_1_q), .clk(CLK), .clr(CLR));  // open: load, D, count, carry
  Multiplexer #(.select(2), .width(4), .enable("false")) multiplexer_1 (
    .in0({Data[3], Addr_B}), .in1(ALU), .in2(Port_A), .out(multiplexer_1_out), .sel(RSS));  // open: in3
  ROM #(.dataWidth(16)) rom_1 (
    .addr(counter_1_q), .data({Opcode, rom_1_data[11], Addr_D, rom_1_data[7], Addr_A, Data[3], Addr_B}));  // open: sel
  ROM #(.addrWidth(4)) rom_2 (.addr(Opcode), .data({rom_2_data[7], SUB, AFS, RSS, DWE, WE}));  // open: sel
  _3_Port_Register u_3_port_register_1 (
    .Input(multiplexer_1_out), .Clock_input(CLK), .WE(WE), .A(Addr_A), .D1(Addr_D), .B(Addr_B),
    .out_7(Port_A), .out_8(Port_B));
  TTY tty_1 (.data({Port_A[2:0], Port_B}), .clk(CLK), .we(DWE), .clr(CLR));
  ALU alu_1 (.A(Port_A), .B(Port_B), .OUT(ALU), .S(AFS), .Sub(SUB));

  // Other names for the same wires on the sheet: Data[2:0] = Addr_B

  // Notes on the sheet:
  //   contents of rom_1 (hex, n*v repeats v):
  //   1004 1108 3001 1206 1305 3023 1406 150c 3045 3045 1606 170f 3067 1002 1100 1102 120c 3012 3001 1104
  //   1202 3012 1304 140a 3034 1102 1202 3012 1100 120a 3012 0 1103 1203 3012 1102 120b 3012 1103 1204
  //   3012 1103 120d 3012 1203 1304 7423 3014 1100 120a 3012 1203 1303 3023 1202 130a 3023 1203 1303 3023
  //   1103 120d 3012 1203 1303 1403 7523 7645 3016 1100 120a 3012 1203 1304 3023 1202 130d 3023 1103 1203
  //   3012 1103 120d 3012 1204 1301 1403 4534 7635 7762 3017
  //   contents of rom_2 (hex, n*v repeats v):
  //   0 1 9 2 5 15 25 35 7*0 75
endmodule

module OR (
  input  [3:0] in_1,
  input  [3:0] in_2,
  output [3:0] out_3
);

  or or_1 (out_3[0], in_1[0], in_2[0]);
  or or_2 (out_3[1], in_1[1], in_2[1]);
  or or_3 (out_3[2], in_1[2], in_2[2]);
  or or_4 (out_3[3], in_1[3], in_2[3]);

  // Other names for the same wires on the sheet: A0 = in_1[0]; A1 = in_1[1]; A2 = in_1[2]; A3 = in_1[3]; B0 = in_2[0];
  //   B1 = in_2[1]; B2 = in_2[2]; B3 = in_2[3]
endmodule

module AND (
  input  [3:0] in_1,
  input  [3:0] in_2,
  output [3:0] out_3
);

  and and_1 (out_3[0], in_1[0], in_2[0]);
  and and_2 (out_3[1], in_1[1], in_2[1]);
  and and_3 (out_3[2], in_1[2], in_2[2]);
  and and_4 (out_3[3], in_1[3], in_2[3]);

  // Other names for the same wires on the sheet: A0 = in_1[0]; A1 = in_1[1]; A2 = in_1[2]; A3 = in_1[3]; B0 = in_2[0];
  //   B1 = in_2[1]; B2 = in_2[2]; B3 = in_2[3]
endmodule

module XOR (
  input  [3:0] in_1,
  input  [3:0] in_2,
  output [3:0] out_3
);

  xor xor_1 (out_3[3], in_1[3], in_2[3]);
  xor xor_2 (out_3[2], in_1[2], in_2[2]);
  xor xor_3 (out_3[1], in_1[1], in_2[1]);
  xor xor_4 (out_3[0], in_1[0], in_2[0]);

  // Other names for the same wires on the sheet: A3 = in_1[0]; A2 = in_1[1]; A1 = in_1[2]; A0 = in_1[3]; B3 = in_2[0];
  //   B2 = in_2[1]; B1 = in_2[2]; B0 = in_2[3]
endmodule

module _1Bit_Adder (
  input  A,
  input  B,
  input  Cin,
  output S,
  output Cout
);

  wire and_1_out, and_2_out, and_3_out;

  xor xor_1 (S, A, B, Cin);
  and and_1 (and_1_out, A, B);
  and and_2 (and_2_out, B, Cin);
  and and_3 (and_3_out, Cin, A);
  or or_1 (Cout, and_1_out, and_2_out, and_3_out);
endmodule

// Adder
module _4Bit_Adder (
  input  [3:0] A,
  input  [3:0] B,
  input  Sub,
  output Out_0,
  output Out_1,
  output Out_2,
  output Out_3
);

  wire C0, C1, C2, n1bit_adder_4_cout, xor_1_out, xor_2_out, xor_3_out, xor_4_out;

  xor xor_1 (xor_1_out, B[0], Sub);
  xor xor_2 (xor_2_out, B[1], Sub);
  xor xor_3 (xor_3_out, B[2], Sub);
  xor xor_4 (xor_4_out, B[3], Sub);
  _1Bit_Adder u_1bit_adder_1 (.A(A[0]), .B(xor_1_out), .Cin(Sub), .S(Out_0), .Cout(C0));
  _1Bit_Adder u_1bit_adder_2 (.A(A[1]), .B(xor_2_out), .Cin(C0), .S(Out_1), .Cout(C1));
  _1Bit_Adder u_1bit_adder_3 (.A(A[2]), .B(xor_3_out), .Cin(C1), .S(Out_2), .Cout(C2));
  _1Bit_Adder u_1bit_adder_4 (.A(A[3]), .B(xor_4_out), .Cin(C2), .S(Out_3), .Cout(n1bit_adder_4_cout));
  // also tied to GND on the sheet: n1bit_adder_4_cout
endmodule

module ALU (
  input  [3:0] A,
  input  [3:0] B,
  input  Sub,
  input  [1:0] S,
  output [3:0] OUT
);

  wire [3:0] and_1_out_3, n4bit_adder_1_out_0, or_1_out_3, xor_1_out_3;

  XOR xor_1 (.in_1(A), .in_2(B), .out_3(xor_1_out_3));
  AND and_1 (.in_1(A), .in_2(B), .out_3(and_1_out_3));
  OR or_1 (.in_1(A), .in_2(B), .out_3(or_1_out_3));
  _4Bit_Adder u_4bit_adder_1 (
    .A(A), .B(B), .Out_0(n4bit_adder_1_out_0[0]), .Sub(Sub), .Out_1(n4bit_adder_1_out_0[1]),
    .Out_2(n4bit_adder_1_out_0[2]), .Out_3(n4bit_adder_1_out_0[3]));
  Multiplexer #(.select(2), .width(4), .enable("false")) multiplexer_1 (
    .in0(xor_1_out_3), .in1(and_1_out_3), .in2(or_1_out_3), .in3(n4bit_adder_1_out_0), .out(OUT), .sel(S));
endmodule

module _3_Port_Register (
  input  [3:0] Input,
  input  Clock_input,
  input  WE,
  input  [2:0] A,
  input  [2:0] B,
  input  [2:0] D1,
  output [3:0] out_7,
  output [3:0] out_8
);

  wire decoder_1_out_0, decoder_1_out_1, decoder_1_out_2, decoder_1_out_3, decoder_1_out_4, decoder_1_out_5,
       decoder_1_out_6, decoder_1_out_7;
  wire [3:0] Output_0, Output_1, Output_2, Output_3, Output_4, Output_5, Output_6, Output_7;

  Decoder decoder_1 (
    .A0(D1[0]), .A1(D1[1]), .A2(D1[2]), .WE(WE), .Out_0(decoder_1_out_0), .Out_1(decoder_1_out_1),
    .Out_2(decoder_1_out_2), .Out_3(decoder_1_out_3), .Out_4(decoder_1_out_4), .Out_5(decoder_1_out_5),
    .Out_6(decoder_1_out_6), .Out_7(decoder_1_out_7));
  _4Bit_Register u_4bit_register_1 (
    .ln_0(Input[0]), .ln_1(Input[1]), .ln_2(Input[2]), .ln_3(Input[3]), .CLK(Clock_input),
    .WE(decoder_1_out_0), .Out_0(Output_0[0]), .Out_1(Output_0[1]), .Out_2(Output_0[2]), .Out_3(Output_0[3]));
  _4Bit_Register u_4bit_register_2 (
    .ln_0(Input[0]), .ln_1(Input[1]), .ln_2(Input[2]), .ln_3(Input[3]), .CLK(Clock_input),
    .WE(decoder_1_out_2), .Out_0(Output_2[0]), .Out_1(Output_2[1]), .Out_2(Output_2[2]), .Out_3(Output_2[3]));
  _4Bit_Register u_4bit_register_3 (
    .ln_0(Input[0]), .ln_1(Input[1]), .ln_2(Input[2]), .ln_3(Input[3]), .CLK(Clock_input),
    .WE(decoder_1_out_4), .Out_0(Output_4[0]), .Out_1(Output_4[1]), .Out_2(Output_4[2]), .Out_3(Output_4[3]));
  _4Bit_Register u_4bit_register_4 (
    .ln_0(Input[0]), .ln_1(Input[1]), .ln_2(Input[2]), .ln_3(Input[3]), .CLK(Clock_input),
    .WE(decoder_1_out_6), .Out_0(Output_6[0]), .Out_1(Output_6[1]), .Out_2(Output_6[2]), .Out_3(Output_6[3]));
  _4Bit_Register u_4bit_register_5 (
    .ln_0(Input[0]), .ln_1(Input[1]), .ln_2(Input[2]), .ln_3(Input[3]), .CLK(Clock_input),
    .WE(decoder_1_out_1), .Out_0(Output_1[0]), .Out_1(Output_1[1]), .Out_2(Output_1[2]), .Out_3(Output_1[3]));
  _4Bit_Register u_4bit_register_6 (
    .ln_0(Input[0]), .ln_1(Input[1]), .ln_2(Input[2]), .ln_3(Input[3]), .CLK(Clock_input),
    .WE(decoder_1_out_3), .Out_0(Output_3[0]), .Out_1(Output_3[1]), .Out_2(Output_3[2]), .Out_3(Output_3[3]));
  _4Bit_Register u_4bit_register_7 (
    .ln_0(Input[0]), .ln_1(Input[1]), .ln_2(Input[2]), .ln_3(Input[3]), .CLK(Clock_input),
    .WE(decoder_1_out_5), .Out_0(Output_5[0]), .Out_1(Output_5[1]), .Out_2(Output_5[2]), .Out_3(Output_5[3]));
  _4Bit_Register u_4bit_register_8 (
    .ln_0(Input[0]), .ln_1(Input[1]), .ln_2(Input[2]), .ln_3(Input[3]), .CLK(Clock_input),
    .WE(decoder_1_out_7), .Out_0(Output_7[0]), .Out_1(Output_7[1]), .Out_2(Output_7[2]), .Out_3(Output_7[3]));
  Multiplexer #(.select(3), .width(4), .enable("false")) multiplexer_1 (
    .in0(Output_0), .in1(Output_1), .in2(Output_2), .in3(Output_3), .in4(Output_4), .in5(Output_5),
    .in6(Output_6), .in7(Output_7), .out(out_7), .sel(A));
  Multiplexer #(.select(3), .width(4), .enable("false")) multiplexer_2 (
    .in0(Output_0), .in1(Output_1), .in2(Output_2), .in3(Output_3), .in4(Output_4), .in5(Output_5),
    .in6(Output_6), .in7(Output_7), .out(out_8), .sel(B));

  // Other names for the same wires on the sheet: CLK = Clock_input
endmodule

module _1_Bit_register (
  input  CLK,
  input  Data_In,
  input  WE,
  output Data_Out
);

  wire multiplexer_1_out;

  Multiplexer #(.enable("false")) multiplexer_1 (.in0(Data_Out), .in1(Data_In), .out(multiplexer_1_out), .sel(WE));
  D_Flip_Flop d_ff_1 (.clk(CLK), .D(multiplexer_1_out), .Q(Data_Out));  // open: Qn, preset, en, reset
endmodule

module _4Bit_Register (
  input  ln_0,
  input  ln_1,
  input  ln_2,
  input  ln_3,
  input  CLK,
  input  WE,
  output Out_0,
  output Out_1,
  output Out_2,
  output Out_3
);

  _1_Bit_register u_1_bit_register_1 (.CLK(CLK), .Data_In(ln_0), .Data_Out(Out_0), .WE(WE));
  _1_Bit_register u_1_bit_register_2 (.CLK(CLK), .Data_In(ln_1), .Data_Out(Out_1), .WE(WE));
  _1_Bit_register u_1_bit_register_3 (.CLK(CLK), .Data_In(ln_2), .Data_Out(Out_2), .WE(WE));
  _1_Bit_register u_1_bit_register_4 (.CLK(CLK), .Data_In(ln_3), .Data_Out(Out_3), .WE(WE));
endmodule

module Decoder (
  input  A0,
  input  A1,
  input  A2,
  input  WE,
  output Out_0,
  output Out_1,
  output Out_2,
  output Out_3,
  output Out_4,
  output Out_5,
  output Out_6,
  output Out_7
);

  wire not_1_out, not_2_out, not_3_out;

  not not_1 (not_1_out, A0);
  not not_2 (not_2_out, A1);
  not not_3 (not_3_out, A2);
  and _0 (Out_0, not_1_out, not_2_out, not_3_out, WE);
  and _1 (Out_1, A0, not_2_out, not_3_out, WE);
  and _2 (Out_2, not_1_out, A1, not_3_out, WE);
  and _3 (Out_3, A0, A1, not_3_out, WE);
  and _4 (Out_4, not_1_out, not_2_out, A2, WE);
  and _5 (Out_5, A0, not_2_out, A2, WE);
  and _6 (Out_6, not_1_out, A1, A2, WE);
  and _7 (Out_7, A0, A1, A2, WE);
endmodule
