// Logisim project Final.circ as structural Verilog: 11 circuits, main circuit main
module main (
  input  CLR
);

  wire CLK, DWE, SUB, WE;
  wire [1:0] AFS, RSS;
  wire [2:0] Addr_A, Addr_B, Addr_D;
  wire [3:0] ALU, multiplexer_1_out, Opcode, Port_A, Port_B;
  wire [3:3] Data;
  wire [7:0] counter_1_q;
  wire [7:7] rom_2_data;
  wire [11:7] rom_1_data;

  Clock clock_1 (.out(CLK));
  Counter counter_1 (.Q(counter_1_q), .clk(CLK), .clr(CLR));  // open: load, D, count, carry
  Multiplexer #(.select(2), .width(4), .enable("false")) multiplexer_1 (
    .in0({Data[3], Addr_B}), .in1(ALU), .in2(Port_A), .out(multiplexer_1_out), .sel(RSS));  // open: in3
  ROM #(.dataWidth(16)) rom_1 (
    .addr(counter_1_q), .data({Opcode, rom_1_data[11], Addr_D, rom_1_data[7], Addr_A, Data[3], Addr_B}));  // open: sel
  ROM #(.addrWidth(4)) rom_2 (.addr(Opcode), .data({rom_2_data[7], SUB, AFS, RSS, DWE, WE}));  // open: sel
  _3_Port_Register u_3_port_register_1 (
    .Input(multiplexer_1_out), .Clock_input(CLK), .WE(WE), .A(Addr_A), .D1(Addr_D), .B(Addr_B),
    .out_7(Port_A), .out_8(Port_B));
  TTY tty_1 (.clk(CLK));  // open: data, we, clr
  ALU alu_1 ();  // open: in_1, in_2, S0, S1, OUT_0, OUT_1, OUT_2, OUT_3

  // Other names for the same wires on the sheet: Data[2:0] = Addr_B
endmodule

module OR (
  input  [3:0] in_1,
  input  [3:0] in_2,
  output [3:0] out_3
);

  or or_1 (out_3[0], in_1[3], in_2[3]);
  or or_2 (out_3[1], in_1[2], in_2[2]);
  or or_3 (out_3[2], in_1[1], in_2[1]);
  or or_4 (out_3[3], in_1[0], in_2[0]);

  // Other names for the same wires on the sheet: A3 = in_1[0]; A2 = in_1[1]; A1 = in_1[2]; A0 = in_1[3]; B3 = in_2[0];
  //   B2 = in_2[1]; B1 = in_2[2]; B0 = in_2[3]
endmodule

module AND (
  input  [3:0] in_1,
  input  [3:0] in_2,
  output [3:0] out_3
);

  and and_1 (out_3[0], in_1[3], in_2[3]);
  and and_2 (out_3[1], in_1[2], in_2[2]);
  and and_3 (out_3[2], in_1[1], in_2[1]);
  and and_4 (out_3[3], in_1[0], in_2[0]);

  // Other names for the same wires on the sheet: A3 = in_1[0]; A2 = in_1[1]; A1 = in_1[2]; A0 = in_1[3]; B3 = in_2[0];
  //   B2 = in_2[1]; B1 = in_2[2]; B0 = in_2[3]
endmodule

module XOR (
  input  [3:0] in_1,
  input  [3:0] in_2,
  output [3:0] out_3
);

  xor xor_1 (out_3[3], in_1[3], in_2[3]);
  xor xor_2 (out_3[2], in_1[2], in_2[2]);
  xor xor_3 (out_3[1], in_1[1], in_2[1]);
  xor xor_4 (out_3[0], in_1[0], in_2[0]);

  // Other names for the same wires on the sheet: A3 = in_1[0]; A2 = in_1[1]; A1 = in_1[2]; A0 = in_1[3]; B3 = in_2[0];
  //   B2 = in_2[1]; B1 = in_2[2]; B0 = in_2[3]
endmodule

module _1Bit_Adder (
  input  A,
  input  B,
  input  Cin,
  output S,
  output Cout
);

  wire and_1_out, and_2_out, and_3_out;

  xor xor_1 (S, A, B, Cin);
  and and_1 (and_1_out, A, B);
  and and_2 (and_2_out, B, Cin);
  and and_3 (and_3_out, Cin, A);
  or or_1 (Cout, and_1_out, and_2_out, and_3_out);
endmodule

// Adder
module _4Bit_Adder (
  input  [3:0] A,
  input  [3:0] B,
  output Out_0,
  output Out_1,
  output Out_2,
  output Out_3
);

  wire C0, C1, C2;

  _1Bit_Adder u_1bit_adder_1 (.A(A[0]), .B(B[0]), .Cin(1'b0), .S(Out_0), .Cout(C0));
  _1Bit_Adder u_1bit_adder_2 (.A(A[1]), .B(B[1]), .Cin(C0), .S(Out_1), .Cout(C1));
  _1Bit_Adder u_1bit_adder_3 (.A(A[2]), .B(B[2]), .Cin(C1), .S(Out_2), .Cout(C2));
  _1Bit_Adder u_1bit_adder_4 (.A(A[3]), .B(B[3]), .Cin(C2), .S(Out_3));  // open: Cout
endmodule

module ALU (
  input  in_1,
  input  in_2,
  input  S0,
  input  S1,
  output OUT_0,
  output OUT_1,
  output OUT_2,
  output OUT_3
);

  wire ADD_0, ADD_1, ADD_2, ADD_3, AND_0, AND_1, AND_2, AND_3, OR_0, OR_1, OR_2, OR_3, XOR_0, XOR_1, XOR_2,
       XOR_3;
  wire [3:0] A, B;

  XOR u_xor_1 (.in_1(A), .in_2(B), .out_3({XOR_0, XOR_1, XOR_2, XOR_3}));
  AND u_and_1 (.in_1(A), .in_2(B), .out_3({AND_3, AND_2, AND_1, AND_0}));
  OR u_or_1 (.in_1(A), .in_2(B), .out_3({OR_3, OR_2, OR_1, OR_0}));
  _4Bit_Adder u_4bit_adder_1 (.Out_0(ADD_0), .Out_1(ADD_1), .Out_2(ADD_2), .Out_3(ADD_3));  // open: A, B
  Multiplexer #(.select(2), .enable("false")) multiplexer_1 (
    .in0(XOR_0), .in1(AND_0), .in2(OR_0), .in3(ADD_0), .out(OUT_0), .sel({S1, S0}));
  Multiplexer #(.select(2), .enable("false")) multiplexer_2 (
    .in0(XOR_1), .in1(AND_1), .in2(OR_1), .in3(ADD_1), .out(OUT_1), .sel({S1, S0}));
  Multiplexer #(.select(2), .enable("false")) multiplexer_3 (
    .in0(XOR_2), .in1(AND_2), .in2(OR_2), .in3(ADD_2), .out(OUT_2), .sel({S1, S0}));
  Multiplexer #(.select(2), .enable("false")) multiplexer_4 (
    .in0(XOR_3), .in1(AND_3), .in2(OR_3), .in3(ADD_3), .out(OUT_3), .sel({S1, S0}));
endmodule

module _3_Port_Register (
  input  [3:0] Input,
  input  Clock_input,
  input  WE,
  input  [2:0] A,
  input  [2:0] B,
  input  [2:0] D1,
  output [3:0] out_7,
  output [3:0] out_8
);

  wire decoder_1_out_0, decoder_1_out_1, decoder_1_out_2, decoder_1_out_3, decoder_1_out_4, decoder_1_out_5,
       decoder_1_out_6, decoder_1_out_7;
  wire [3:0] Output_0, Output_1, Output_2, Output_3, Output_4, Output_5, Output_6, Output_7;

  Decoder decoder_1 (
    .A0(D1[0]), .A1(D1[1]), .A2(D1[2]), .WE(WE), .Out_0(decoder_1_out_0), .Out_1(decoder_1_out_1),
    .Out_2(decoder_1_out_2), .Out_3(decoder_1_out_3), .Out_4(decoder_1_out_4), .Out_5(decoder_1_out_5),
    .Out_6(decoder_1_out_6), .Out_7(decoder_1_out_7));
  _4Bit_Register u_4bit_register_1 (
    .ln_0(Input[0]), .ln_1(Input[1]), .ln_2(Input[2]), .ln_3(Input[3]), .CLK(Clock_input),
    .WE(decoder_1_out_0), .Out_0(Output_0[0]), .Out_1(Output_0[1]), .Out_2(Output_0[2]), .Out_3(Output_0[3]));
  _4Bit_Register u_4bit_register_2 (
    .ln_0(Input[0]), .ln_1(Input[1]), .ln_2(Input[2]), .ln_3(Input[3]), .CLK(Clock_input),
    .WE(decoder_1_out_2), .Out_0(Output_2[0]), .Out_1(Output_2[1]), .Out_2(Output_2[2]), .Out_3(Output_2[3]));
  _4Bit_Register u_4bit_register_3 (
    .ln_0(Input[0]), .ln_1(Input[1]), .ln_2(Input[2]), .ln_3(Input[3]), .CLK(Clock_input),
    .WE(decoder_1_out_4), .Out_0(Output_4[0]), .Out_1(Output_4[1]), .Out_2(Output_4[2]), .Out_3(Output_4[3]));
  _4Bit_Register u_4bit_register_4 (
    .ln_0(Input[0]), .ln_1(Input[1]), .ln_2(Input[2]), .ln_3(Input[3]), .CLK(Clock_input),
    .WE(decoder_1_out_6), .Out_0(Output_6[0]), .Out_1(Output_6[1]), .Out_2(Output_6[2]), .Out_3(Output_6[3]));
  _4Bit_Register u_4bit_register_5 (
    .ln_0(Input[0]), .ln_1(Input[1]), .ln_2(Input[2]), .ln_3(Input[3]), .CLK(Clock_input),
    .WE(decoder_1_out_1), .Out_0(Output_1[0]), .Out_1(Output_1[1]), .Out_2(Output_1[2]), .Out_3(Output_1[3]));
  _4Bit_Register u_4bit_register_6 (
    .ln_0(Input[0]), .ln_1(Input[1]), .ln_2(Input[2]), .ln_3(Input[3]), .CLK(Clock_input),
    .WE(decoder_1_out_3), .Out_0(Output_3[0]), .Out_1(Output_3[1]), .Out_2(Output_3[2]), .Out_3(Output_3[3]));
  _4Bit_Register u_4bit_register_7 (
    .ln_0(Input[0]), .ln_1(Input[1]), .ln_2(Input[2]), .ln_3(Input[3]), .CLK(Clock_input),
    .WE(decoder_1_out_5), .Out_0(Output_5[0]), .Out_1(Output_5[1]), .Out_2(Output_5[2]), .Out_3(Output_5[3]));
  _4Bit_Register u_4bit_register_8 (
    .ln_0(Input[0]), .ln_1(Input[1]), .ln_2(Input[2]), .ln_3(Input[3]), .CLK(Clock_input),
    .WE(decoder_1_out_7), .Out_0(Output_7[0]), .Out_1(Output_7[1]), .Out_2(Output_7[2]), .Out_3(Output_7[3]));
  Multiplexer #(.select(3), .width(4), .enable("false")) multiplexer_1 (
    .in0(Output_0), .in1(Output_1), .in2(Output_2), .in3(Output_3), .in4(Output_4), .in5(Output_5),
    .in6(Output_6), .in7(Output_7), .out(out_7), .sel(A));
  Multiplexer #(.select(3), .width(4), .enable("false")) multiplexer_2 (
    .in0(Output_0), .in1(Output_1), .in2(Output_2), .in3(Output_3), .in4(Output_4), .in5(Output_5),
    .in6(Output_6), .in7(Output_7), .out(out_8), .sel(B));

  // Other names for the same wires on the sheet: CLK = Clock_input
endmodule

module _1_Bit_register (
  input  CLK,
  input  Data_In,
  input  WE,
  output Data_Out
);

  wire multiplexer_1_out;

  Multiplexer #(.enable("false")) multiplexer_1 (.in0(Data_Out), .in1(Data_In), .out(multiplexer_1_out), .sel(WE));
  D_Flip_Flop d_ff_1 (.clk(CLK), .D(multiplexer_1_out), .Q(Data_Out));  // open: Qn, preset, en, reset
endmodule

module _4Bit_Register (
  input  ln_0,
  input  ln_1,
  input  ln_2,
  input  ln_3,
  input  CLK,
  input  WE,
  output Out_0,
  output Out_1,
  output Out_2,
  output Out_3
);

  _1_Bit_register u_1_bit_register_1 (.CLK(CLK), .Data_In(ln_0), .Data_Out(Out_0), .WE(WE));
  _1_Bit_register u_1_bit_register_2 (.CLK(CLK), .Data_In(ln_1), .Data_Out(Out_1), .WE(WE));
  _1_Bit_register u_1_bit_register_3 (.CLK(CLK), .Data_In(ln_2), .Data_Out(Out_2), .WE(WE));
  _1_Bit_register u_1_bit_register_4 (.CLK(CLK), .Data_In(ln_3), .Data_Out(Out_3), .WE(WE));
endmodule

module Decoder (
  input  A0,
  input  A1,
  input  A2,
  input  WE,
  output Out_0,
  output Out_1,
  output Out_2,
  output Out_3,
  output Out_4,
  output Out_5,
  output Out_6,
  output Out_7
);

  wire not_1_out, not_2_out, not_3_out;

  not not_1 (not_1_out, A0);
  not not_2 (not_2_out, A1);
  not not_3 (not_3_out, A2);
  and _0 (Out_0, not_1_out, not_2_out, not_3_out, WE);
  and _1 (Out_1, A0, not_2_out, not_3_out, WE);
  and _2 (Out_2, not_1_out, A1, not_3_out, WE);
  and _3 (Out_3, A0, A1, not_3_out, WE);
  and _4 (Out_4, not_1_out, not_2_out, A2, WE);
  and _5 (Out_5, A0, not_2_out, A2, WE);
  and _6 (Out_6, not_1_out, A1, A2, WE);
  and _7 (Out_7, A0, A1, A2, WE);
endmodule
