// Logisim project Graycode_2b_Counter-replace.circ as structural Verilog: 1 circuit, main circuit main
module main (
  input  Increment,
  input  Clock_Input,
  output Out_0,
  output Out_1
);

  wire and_1_out, and_2_out, and_3_out, and_4_out, and_5_out, and_6_out, INC_prime, or_1_out, or_2_out,
       Q0_prime, Q1_prime;

  not not_1 (INC_prime, Increment);
  and and_1 (and_1_out, Increment, Out_0);
  and and_2 (and_2_out, Out_0, Out_1);
  and and_3 (and_3_out, Out_1, INC_prime);
  and and_4 (and_4_out, Increment, Q0_prime);
  and and_5 (and_5_out, Q0_prime, Out_0);
  and and_6 (and_6_out, Out_0, INC_prime);
  or or_1 (or_1_out, and_1_out, and_2_out, and_3_out);
  or or_2 (or_2_out, and_4_out, and_5_out, and_6_out);
  D_Flip_Flop d_ff_1 (.clk(Clock_Input), .D(or_1_out), .Q(Out_1), .Qn(Q0_prime));  // open: preset, en, reset
  D_Flip_Flop d_ff_2 (.clk(Clock_Input), .D(or_2_out), .Q(Out_0), .Qn(Q1_prime));  // open: preset, en, reset

  // Other names for the same wires on the sheet: CLK = Clock_Input; INC = Increment; Q0 = Out_1; Q1 = Out_0
endmodule
