// Logisim project NAND_Latch.circ as structural Verilog: 1 circuit, main circuit main
module main (
  input  D,
  input  Gate,
  input  D1,
  input  Gate1,
  output out_5,
  output out_6,
  output out_7,
  output out_8
);

  wire and_1_out, and_2_out, nand_1_out, nand_2_out, not_1_out, not_2_out;

  and and_1 (and_1_out, D, Gate);
  and and_2 (and_2_out, Gate, not_1_out);
  not not_1 (not_1_out, D);
  nand nand_1 (nand_1_out, D1, Gate1);
  nand nand_2 (nand_2_out, Gate1, not_2_out);
  not not_2 (not_2_out, D1);
  or or_1 (out_5, and_1_out, ~out_6);  // OR_Gate
  or or_2 (out_6, ~out_5, and_2_out);  // OR_Gate
  nand nand_3 (out_7, nand_1_out, out_8);
  nand nand_4 (out_8, out_7, nand_2_out);

  // Other names for the same wires on the sheet: Q = out_5; Q1 = out_7; Q_prime = out_6; Q_prime_1 = out_8
endmodule
