// Logisim project Ring_Counter-replace.circ as structural Verilog: 1 circuit, main circuit main
module main (
  input  Clock_Input,
  input  Reset,
  output Out_0,
  output Out_1,
  output Out_2
);

  D_Flip_Flop d_ff_1 (.clk(Clock_Input), .D(Out_1), .Q(Out_2), .reset(Reset));  // open: Qn, preset, en
  D_Flip_Flop d_ff_2 (.clk(Clock_Input), .D(Out_0), .Q(Out_1), .reset(Reset));  // open: Qn, preset, en
  D_Flip_Flop d_ff_3 (.clk(Clock_Input), .D(Out_2), .Q(Out_0), .preset(Reset));  // open: Qn, en, reset

  // Other names for the same wires on the sheet: Q0 = Out_0; Q1 = Out_1; Q2 = Out_2
endmodule
