// Logisim project RoadRipper-Gates.circ as structural Verilog: 1 circuit, main circuit main
module main (
  input  Stop,
  input  Left,
  input  Right,
  input  Clock,
  output L_Front,
  output L_Back,
  output R_Front,
  output R_Back
);

  wire and_2_out, and_3_out, and_5_out, and_6_out, not_1_out, not_2_out;

  not not_1 (not_1_out, Left);
  not not_2 (not_2_out, Right);
  and and_1 (L_Front, Clock, Left);
  and and_2 (and_2_out, Right, Stop);
  and and_3 (and_3_out, Stop, not_1_out);
  and and_4 (R_Front, Clock, Right);
  and and_5 (and_5_out, Left, Stop);
  and and_6 (and_6_out, not_2_out, Stop);
  or or_1 (L_Back, L_Front, and_2_out, and_3_out);
  or or_2 (R_Back, R_Front, and_5_out, and_6_out);
endmodule
