// Logisim project SR_SC_D_Latches-replace.circ as structural Verilog: 1 circuit, main circuit main
module main (
  input  S,
  input  R,
  input  S_2,
  input  R_2,
  input  D,
  input  Gate,
  output Q1_prime,
  output Q1,
  output Q2_prime,
  output Q2,
  output Q3_prime,
  output Q3
);

  wire and_1_out, and_2_out, not_1_out;

  nor nor_1 (Q1_prime, S, Q1);
  nor nor_2 (Q1, Q1_prime, R);
  and and_1 (and_1_out, D, Gate);
  not not_1 (not_1_out, D);
  and and_2 (and_2_out, not_1_out, Gate);
  nand nand_1 (Q2, S_2, Q2_prime);
  nand nand_2 (Q2_prime, Q2, R_2);
  nor nor_3 (Q3_prime, and_1_out, Q3);
  nor nor_4 (Q3, Q3_prime, and_2_out);

  // Other names for the same wires on the sheet: G = Gate; Q_prime_1 = Q1_prime; Q_prime_2 = Q2_prime;
  //   Q_prime_3 = Q3_prime; R1 = R; R2 = R_2; S1 = S; S2 = S_2

  // Notes on the sheet:
  //   NOR Latch
  //   NAND Latch
  //   Gated D Latch
endmodule
