// Logisim project TwoBit_2to1_MUX-replace.circ as structural Verilog: 1 circuit, main circuit main
module main (
  input  A0,
  input  A1,
  input  S,
  input  B0,
  input  B1,
  output D0,
  output D1
);

  Multiplexer #(.enable("false")) multiplexer_1 (.in0(A0), .in1(B0), .out(D0), .sel(S));
  Multiplexer #(.enable("false")) multiplexer_2 (.in0(A1), .in1(B1), .out(D1), .sel(S));
endmodule
