// Logisim project Up_Counter-replace.circ as structural Verilog: 1 circuit, main circuit main
module main (
  input  Clock_Input,
  output Out_0,
  output Out_1,
  output Out_2
);

  wire nand_1_out, nand_2_out, nand_3_out, nand_4_out, nand_5_out, nand_6_out, nand_7_out, Q0_prime,
       Q1_prime, Q2_prime;

  nand nand_1 (nand_1_out, Q0_prime, Out_1);
  nand nand_2 (nand_2_out, Out_0, Q1_prime);
  nand nand_3 (nand_3_out, Out_2, Q1_prime);
  nand nand_4 (nand_4_out, Out_2, Q0_prime);
  nand nand_5 (nand_5_out, Q2_prime, Out_1, Out_0);
  nand nand_6 (nand_6_out, nand_1_out, nand_2_out);
  nand nand_7 (nand_7_out, nand_3_out, nand_4_out, nand_5_out);
  D_Flip_Flop d_ff_1 (.clk(Clock_Input), .D(Q0_prime), .Q(Out_0), .Qn(Q0_prime));  // open: preset, en, reset
  D_Flip_Flop d_ff_2 (.clk(Clock_Input), .D(nand_6_out), .Q(Out_1), .Qn(Q1_prime));  // open: preset, en, reset
  D_Flip_Flop d_ff_3 (.clk(Clock_Input), .D(nand_7_out), .Q(Out_2), .Qn(Q2_prime));  // open: preset, en, reset

  // Other names for the same wires on the sheet: CLK = Clock_Input; Q0 = Out_0; Q1 = Out_1; Q2 = Out_2
endmodule
